// Logisim project cpu.circ as structural Verilog: 7 circuits, main circuit main
module main (
  input  reset
);

  wire clk, memory_latch_1_oe_latched, memory_latch_1_we_latched, nclk;
  wire [2:0] Rd, Rs, Rt, Shamt;
  wire [3:0] Opcode;
  wire [15:0] alu_1_aluoutput, alu_2_aluoutput, memory_latch_1_address_latched,
       memory_latch_1_data_in_latched, PC_output_16_bit, regfile_1_r1data, regfile_1_r2data;

  Clock clock_1 (.out(clk));
  not not_1 (nclk, clk);
  OneReg PC (.reset(reset), .clk(nclk), .WEn(1'b1), .input_16_bit(alu_1_aluoutput), .output_16_bit(PC_output_16_bit));
  // Probe on PC_output_16_bit
  ROM #(.addrWidth(16), .dataWidth(16)) rom_1 (.addr(PC_output_16_bit), .data({Opcode, Rs, Rt, Rd, Shamt}));
  alu alu_1 (.A(16'h1), .B(PC_output_16_bit), .OpType(2'b00), .aluOutput(alu_1_aluoutput));
  memory_latch memory_latch_1 (
    .address_latched(memory_latch_1_address_latched), .WE_latched(memory_latch_1_we_latched),
    .OE_latched(memory_latch_1_oe_latched), .data_in_latched(memory_latch_1_data_in_latched));  // open: address, WE, clk, data_in
  // Probe on {Opcode, Rs, Rt, Rd, Shamt}
  RAM #(.addrWidth(16), .dataWidth(16), .trigger("high"), .databus("bibus")) ram_1 (
    .addr(memory_latch_1_address_latched), .we(memory_latch_1_we_latched), .oe(memory_latch_1_oe_latched),
    .din(memory_latch_1_data_in_latched));  // open: dout
  RegFile regfile_1 (
    .reset(reset), .RegWSel(Rd), .clk(clk), .RegR1Sel(Rs), .RegR2Sel(Rt), .DataIn(alu_2_aluoutput),
    .R1Data(regfile_1_r1data), .R2Data(regfile_1_r2data));  // open: RegWE
  alu alu_2 (.A(regfile_1_r1data), .B(regfile_1_r2data), .aluOutput(alu_2_aluoutput));  // open: OpType

  // Notes on the sheet:
  //   Control
endmodule

module memory_latch (
  input  [15:0] address,
  input  WE,
  input  clk,
  input  [15:0] data_in,
  output [15:0] address_latched,
  output WE_latched,
  output OE_latched,
  output [15:0] data_in_latched
);

  wire DMwe_latch_q;
  wire [15:0] addr_latch_q;

  Register #(.width(16), .trigger("falling")) addr_latch (
    .D(address), .en(WE), .clk(clk), .Q(addr_latch_q));  // open: clr
  D_Flip_Flop #(.trigger("falling")) DMwe_latch (.D(WE), .clk(clk), .Q(DMwe_latch_q));  // open: Qn, preset, reset
  Register #(.width(16), .trigger("falling")) data_to_be_written (
    .D(data_in), .en(WE), .clk(clk), .Q(data_in_latched));  // open: clr
  Multiplexer #(.width(16), .enable("false")) multiplexer_1 (
    .in0(address), .in1(addr_latch_q), .out(address_latched), .sel(DMwe_latch_q));
  and and_1 (WE_latched, clk, DMwe_latch_q);
  not not_1 (OE_latched, WE_latched);
endmodule

module OneReg (
  input  reset,
  input  clk,
  input  WEn,
  input  [15:0] input_16_bit,
  output [15:0] output_16_bit
);

  wire clk_enable;

  D_Flip_Flop d_ff_1 (
    .D(input_16_bit[15]), .clk(clk_enable), .Q(output_16_bit[15]), .reset(reset));  // open: Qn, preset
  D_Flip_Flop d_ff_2 (.D(input_16_bit[7]), .clk(clk_enable), .Q(output_16_bit[7]), .reset(reset));  // open: Qn, preset
  D_Flip_Flop d_ff_3 (
    .D(input_16_bit[14]), .clk(clk_enable), .Q(output_16_bit[14]), .reset(reset));  // open: Qn, preset
  D_Flip_Flop d_ff_4 (.D(input_16_bit[6]), .clk(clk_enable), .Q(output_16_bit[6]), .reset(reset));  // open: Qn, preset
  and and_1 (clk_enable, clk, WEn);
  D_Flip_Flop d_ff_5 (
    .D(input_16_bit[13]), .clk(clk_enable), .Q(output_16_bit[13]), .reset(reset));  // open: Qn, preset
  D_Flip_Flop d_ff_6 (.D(input_16_bit[5]), .clk(clk_enable), .Q(output_16_bit[5]), .reset(reset));  // open: Qn, preset
  D_Flip_Flop d_ff_7 (
    .D(input_16_bit[12]), .clk(clk_enable), .Q(output_16_bit[12]), .reset(reset));  // open: Qn, preset
  D_Flip_Flop d_ff_8 (.D(input_16_bit[4]), .clk(clk_enable), .Q(output_16_bit[4]), .reset(reset));  // open: Qn, preset
  D_Flip_Flop d_ff_9 (
    .D(input_16_bit[11]), .clk(clk_enable), .Q(output_16_bit[11]), .reset(reset));  // open: Qn, preset
  D_Flip_Flop d_ff_10 (.D(input_16_bit[3]), .clk(clk_enable), .Q(output_16_bit[3]), .reset(reset));  // open: Qn, preset
  D_Flip_Flop d_ff_11 (
    .D(input_16_bit[10]), .clk(clk_enable), .Q(output_16_bit[10]), .reset(reset));  // open: Qn, preset
  D_Flip_Flop d_ff_12 (.D(input_16_bit[2]), .clk(clk_enable), .Q(output_16_bit[2]), .reset(reset));  // open: Qn, preset
  D_Flip_Flop d_ff_13 (.D(input_16_bit[9]), .clk(clk_enable), .Q(output_16_bit[9]), .reset(reset));  // open: Qn, preset
  D_Flip_Flop d_ff_14 (.D(input_16_bit[1]), .clk(clk_enable), .Q(output_16_bit[1]), .reset(reset));  // open: Qn, preset
  D_Flip_Flop d_ff_15 (.D(input_16_bit[8]), .clk(clk_enable), .Q(output_16_bit[8]), .reset(reset));  // open: Qn, preset
  D_Flip_Flop d_ff_16 (.D(input_16_bit[0]), .clk(clk_enable), .Q(output_16_bit[0]), .reset(reset));  // open: Qn, preset

  // Other names for the same wires on the sheet: enable = WEn; In0 = input_16_bit[0]; In1 = input_16_bit[1];
  //   In2 = input_16_bit[2]; In3 = input_16_bit[3]; In4 = input_16_bit[4]; In5 = input_16_bit[5];
  //   In6 = input_16_bit[6]; In7 = input_16_bit[7]; In8 = input_16_bit[8]; In9 = input_16_bit[9];
  //   In10 = input_16_bit[10]; In11 = input_16_bit[11]; In12 = input_16_bit[12]; In13 = input_16_bit[13];
  //   In14 = input_16_bit[14]; In15 = input_16_bit[15]; R0 = output_16_bit[0]; R1 = output_16_bit[1];
  //   R2 = output_16_bit[2]; R3 = output_16_bit[3]; R4 = output_16_bit[4]; R5 = output_16_bit[5];
  //   R6 = output_16_bit[6]; R7 = output_16_bit[7]; R8 = output_16_bit[8]; R9 = output_16_bit[9];
  //   R10 = output_16_bit[10]; R11 = output_16_bit[11]; R12 = output_16_bit[12]; R13 = output_16_bit[13];
  //   R14 = output_16_bit[14]; R15 = output_16_bit[15]
endmodule

module RegFile (
  input  reset,
  input  [2:0] RegWSel,
  input  clk,
  input  [2:0] RegR1Sel,
  input  RegWE,
  input  [2:0] RegR2Sel,
  input  [15:0] DataIn,
  output [15:0] R1Data,
  output [15:0] R2Data
);

  wire R1_0, R1_1, R1_2, R1_3, R1_4, R1_5, R1_6, R1_7, R2_0, R2_1, R2_2, R2_3, R2_4, R2_5, R2_6, R2_7, WE0,
       WE1, WE2, WE3, WE4, WE5, WE6, WE7;
  wire [15:0] Q0, Q1, Q2, Q3, Q4, Q5, Q6, Q7;

  assign R1Data = R1_7 ? Q7 : 16'bz;  // Controlled_Buffer controlled_buffer_1
  assign R1Data = R1_6 ? Q6 : 16'bz;  // Controlled_Buffer controlled_buffer_2
  assign R1Data = R1_5 ? Q5 : 16'bz;  // Controlled_Buffer controlled_buffer_3
  assign R1Data = R1_4 ? Q4 : 16'bz;  // Controlled_Buffer controlled_buffer_4
  assign R1Data = R1_3 ? Q3 : 16'bz;  // Controlled_Buffer controlled_buffer_5
  assign R1Data = R1_2 ? Q2 : 16'bz;  // Controlled_Buffer controlled_buffer_6
  assign R1Data = R1_1 ? Q1 : 16'bz;  // Controlled_Buffer controlled_buffer_7
  assign R1Data = R1_0 ? Q0 : 16'bz;  // Controlled_Buffer controlled_buffer_8
  OneReg reg7 (.reset(reset), .clk(clk), .WEn(WE7), .input_16_bit(DataIn), .output_16_bit(Q7));
  OneReg reg3 (.reset(reset), .clk(clk), .WEn(WE3), .input_16_bit(DataIn), .output_16_bit(Q3));
  assign R2Data = R2_7 ? Q7 : 16'bz;  // Controlled_Buffer controlled_buffer_9
  assign R2Data = R2_6 ? Q6 : 16'bz;  // Controlled_Buffer controlled_buffer_10
  assign R2Data = R2_5 ? Q5 : 16'bz;  // Controlled_Buffer controlled_buffer_11
  assign R2Data = R2_4 ? Q4 : 16'bz;  // Controlled_Buffer controlled_buffer_12
  assign R2Data = R2_3 ? Q3 : 16'bz;  // Controlled_Buffer controlled_buffer_13
  assign R2Data = R2_2 ? Q2 : 16'bz;  // Controlled_Buffer controlled_buffer_14
  assign R2Data = R2_1 ? Q1 : 16'bz;  // Controlled_Buffer controlled_buffer_15
  assign R2Data = R2_0 ? Q0 : 16'bz;  // Controlled_Buffer controlled_buffer_16
  OneReg reg6 (.reset(reset), .clk(clk), .WEn(WE6), .input_16_bit(DataIn), .output_16_bit(Q6));
  OneReg reg2 (.reset(reset), .clk(clk), .WEn(WE2), .input_16_bit(DataIn), .output_16_bit(Q2));
  Decoder #(.select(3)) decoder_1 (
    .out0(WE0), .out1(WE1), .out2(WE2), .out3(WE3), .out4(WE4), .out5(WE5), .out6(WE6), .out7(WE7),
    .sel(RegWSel), .en(RegWE));
  Decoder #(.select(3)) decoder_2 (
    .out0(R1_0), .out1(R1_1), .out2(R1_2), .out3(R1_3), .out4(R1_4), .out5(R1_5), .out6(R1_6), .out7(R1_7),
    .sel(RegR1Sel));  // open: en
  OneReg reg5 (.reset(reset), .clk(clk), .WEn(WE5), .input_16_bit(DataIn), .output_16_bit(Q5));
  OneReg reg1 (.reset(reset), .clk(clk), .WEn(WE1), .input_16_bit(DataIn), .output_16_bit(Q1));
  Decoder #(.select(3)) decoder_3 (
    .out0(R2_0), .out1(R2_1), .out2(R2_2), .out3(R2_3), .out4(R2_4), .out5(R2_5), .out6(R2_6), .out7(R2_7),
    .sel(RegR2Sel));  // open: en
  OneReg reg0 (.reset(reset), .clk(clk), .WEn(1'b0), .input_16_bit({16{1'b0}}), .output_16_bit(Q0));
  OneReg reg4 (.reset(reset), .clk(clk), .WEn(WE4), .input_16_bit(DataIn), .output_16_bit(Q4));

  // Other names for the same wires on the sheet: Data[15:0] = DataIn
endmodule

module alu (
  input  [15:0] A,
  input  [15:0] B,
  input  [1:0] OpType,
  output [15:0] aluOutput
);

  wire [15:0] add, not_not, or_or, sub;

  add_circuit add_circuit_1 (.B(B), .A(A), .sub(1'b0), .result(add));
  add_circuit add_circuit_2 (.B(B), .A(A), .sub(1'b1), .result(sub));
  assign or_or = A | B;  // OR_Gate or_1, 16 bits wide
  assign not_not = ~A;  // NOT_Gate not_1, 16 bits wide
  Multiplexer #(.select(2), .width(16), .enable("false")) multiplexer_1 (
    .in0(add), .in1(sub), .in2(or_or), .in3(not_not), .out(aluOutput), .sel(OpType));

  // Other names for the same wires on the sheet: output_output[15:0] = aluOutput

  // Notes on the sheet:
  //   ALU I/O
  //   ALU math and logic
  //   ALU Selector
endmodule

module add_circuit (
  input  [15:0] B,
  input  [15:0] A,
  input  sub,
  output [15:0] result
);

  wire C14, C15, full_adder_3_cout, full_adder_4_cout, full_adder_5_cout, full_adder_6_cout,
       full_adder_7_cout, full_adder_8_cout, full_adder_9_cout, full_adder_10_cout, full_adder_11_cout,
       full_adder_12_cout, full_adder_13_cout, full_adder_14_cout, full_adder_15_cout, full_adder_16_cout,
       xor_1_out, xor_2_out, xor_3_out, xor_4_out, xor_5_out, xor_6_out, xor_7_out, xor_8_out, xor_9_out,
       xor_10_out, xor_11_out, xor_12_out, xor_13_out, xor_14_out, xor_15_out, xor_16_out;

  full_adder full_adder_1 (.Cin(C14), .a(A[15]), .b(xor_1_out), .Sum(result[15]), .Cout(C15));
  xor xor_1 (xor_1_out, sub, B[15]);
  full_adder full_adder_2 (.Cin(full_adder_3_cout), .a(A[14]), .b(xor_2_out), .Sum(result[14]), .Cout(C14));
  xor xor_2 (xor_2_out, sub, B[14]);
  full_adder full_adder_3 (
    .Cin(full_adder_4_cout), .a(A[13]), .b(xor_3_out), .Sum(result[13]), .Cout(full_adder_3_cout));
  xor xor_3 (xor_3_out, sub, B[13]);
  full_adder full_adder_4 (
    .Cin(full_adder_5_cout), .a(A[12]), .b(xor_4_out), .Sum(result[12]), .Cout(full_adder_4_cout));
  xor xor_4 (xor_4_out, sub, B[12]);
  full_adder full_adder_5 (
    .Cin(full_adder_6_cout), .a(A[11]), .b(xor_5_out), .Sum(result[11]), .Cout(full_adder_5_cout));
  xor xor_5 (xor_5_out, sub, B[11]);
  full_adder full_adder_6 (
    .Cin(full_adder_7_cout), .a(A[10]), .b(xor_6_out), .Sum(result[10]), .Cout(full_adder_6_cout));
  xor xor_6 (xor_6_out, sub, B[10]);
  full_adder full_adder_7 (.Cin(full_adder_8_cout), .a(A[9]), .b(xor_7_out), .Sum(result[9]), .Cout(full_adder_7_cout));
  xor xor_7 (xor_7_out, sub, B[9]);
  full_adder full_adder_8 (.Cin(full_adder_9_cout), .a(A[8]), .b(xor_8_out), .Sum(result[8]), .Cout(full_adder_8_cout));
  xor xor_8 (xor_8_out, sub, B[8]);
  full_adder full_adder_9 (
    .Cin(full_adder_10_cout), .a(A[7]), .b(xor_9_out), .Sum(result[7]), .Cout(full_adder_9_cout));
  xor xor_9 (xor_9_out, sub, B[7]);
  full_adder full_adder_10 (
    .Cin(full_adder_11_cout), .a(A[6]), .b(xor_10_out), .Sum(result[6]), .Cout(full_adder_10_cout));
  xor xor_10 (xor_10_out, sub, B[6]);
  full_adder full_adder_11 (
    .Cin(full_adder_12_cout), .a(A[5]), .b(xor_11_out), .Sum(result[5]), .Cout(full_adder_11_cout));
  xor xor_11 (xor_11_out, sub, B[5]);
  full_adder full_adder_12 (
    .Cin(full_adder_13_cout), .a(A[4]), .b(xor_12_out), .Sum(result[4]), .Cout(full_adder_12_cout));
  xor xor_12 (xor_12_out, sub, B[4]);
  full_adder full_adder_13 (
    .Cin(full_adder_14_cout), .a(A[3]), .b(xor_13_out), .Sum(result[3]), .Cout(full_adder_13_cout));
  xor xor_13 (xor_13_out, sub, B[3]);
  full_adder full_adder_14 (
    .Cin(full_adder_15_cout), .a(A[2]), .b(xor_14_out), .Sum(result[2]), .Cout(full_adder_14_cout));
  xor xor_14 (xor_14_out, sub, B[2]);
  full_adder full_adder_15 (
    .Cin(full_adder_16_cout), .a(A[1]), .b(xor_15_out), .Sum(result[1]), .Cout(full_adder_15_cout));
  xor xor_15 (xor_15_out, sub, B[1]);
  full_adder full_adder_16 (.Cin(sub), .a(A[0]), .b(xor_16_out), .Sum(result[0]), .Cout(full_adder_16_cout));
  xor xor_16 (xor_16_out, sub, B[0]);

  // Other names for the same wires on the sheet: s0 = result[0]; s1 = result[1]; s2 = result[2]; s3 = result[3];
  //   s4 = result[4]; s5 = result[5]; s6 = result[6]; s7 = result[7]; s8 = result[8]; s9 = result[9];
  //   s10 = result[10]; s11 = result[11]; s12 = result[12]; s13 = result[13]; s14 = result[14]; s15 = result[15]
endmodule

module full_adder (
  input  Cin,
  input  a,
  input  b,
  output Sum,
  output Cout
);

  wire and_1_out, and_2_out, xor_1_out;

  and and_1 (and_1_out, b, a);
  xor xor_1 (xor_1_out, a, b);
  or or_1 (Cout, and_1_out, and_2_out);
  and and_2 (and_2_out, xor_1_out, Cin);
  xor xor_2 (Sum, Cin, xor_1_out);
endmodule
